# Fritzing sketch pico-asynchronous-neo-pixels (saved by Fritzing 1.0.3b)
breadboards: 1

parts:
  Mod1 = Raspberry Pi Pico
  NEOPIXEL1 = Neopixel Strip -- Black (30/m) [part_number=1376]
  S1 = Momentary Switch [package=ksa_sealed_tac_switch]
  S2 = Momentary Switch [package=ksa_sealed_tac_switch]
  S3 = Momentary Switch [package=ksa_sealed_tac_switch]

nets:
  N1: Mod1.pin_1, NEOPIXEL1.Din
  N2: Mod1.pin_2, S1.2
  N3: Mod1.pin_3, Mod1.pin_8, Mod1.pin_13, Mod1.pin_18, Mod1.pin_23, Mod1.pin_28, Mod1.pin_33, Mod1.pin_38, Mod1.pin_42, NEOPIXEL1.GND
  N4: Mod1.pin_4, S2.2
  N5: Mod1.pin_5, S3.2
  N6: Mod1.pin_36, S1.3, S2.3, S3.3
  N7: Mod1.pin_39, NEOPIXEL1.+5V

custom parts:
  Raspberry Pi Pico: Raspberry Pi Pico. Based around the RP2040 microcontroller the Pico is a low cost microcontroller device bringing Raspberry Pi quality, cost, and easy of use to the microcontroller space. Jan 2021, Split part in to two versions: tht (this one) and SMD. This one will drill holes for a .1 in header in pcb to allow plugging in the module as well as providing pads to solder the module to the top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
  Neopixel Strip -- Black (30/m): These NeoPixel strips have 30 digitally-addressable pixel LEDs per meter and are very affordable and are only 12.5 mm wide, 10 mm if you remove the strip from the casing.
